// Digital circuit ALU.dig as structural Verilog
module ALU (
  input  [7:0] AC_in,
  input  [7:0] N,
  input  [2:0] SEL,
  input  CLK,
  output [7:0] AC,
  output [7:0] MQ
);

  wire [7:0] divisor_8bits_1_mq, divisor_8bits_1_resto, multiplexer_1_out, multiplexer_2_out,
       multiplicador_8bits_1_ac, multiplicador_8bits_1_mq, shift_left_1_ac, shift_right_1_ac,
       somador_8bits_1_s, subtrator_8bits_1_s;

  somador_8bits somador_8bits_1 (.Cin(1'b0), .A(AC_in), .B(N), .S(somador_8bits_1_s));  // open: Cout
  subtrator_8bits subtrator_8bits_1 (.A(AC_in), .B(N), .S(subtrator_8bits_1_s));  // open: Cout
  multiplicador_8bits multiplicador_8bits_1 (
    .A(AC_in), .B(N), .AC(multiplicador_8bits_1_ac), .MQ(multiplicador_8bits_1_mq));  // open: S
  divisor_8bits divisor_8bits_1 (.AC(AC_in), .N(N), .Resto(divisor_8bits_1_resto), .MQ(divisor_8bits_1_mq));
  shift_left shift_left_1 (.AC_in(AC_in), .AC(shift_left_1_ac));
  shift_right shift_right_1 (.AC_in(AC_in), .AC(shift_right_1_ac));
  Multiplexer #(.Selector_Bits(3), .Bits(8)) multiplexer_1 (
    .sel(SEL), .in_0(somador_8bits_1_s), .in_1(subtrator_8bits_1_s), .in_2(multiplicador_8bits_1_ac),
    .in_3(divisor_8bits_1_resto), .in_4(shift_left_1_ac), .in_5(shift_right_1_ac), .in_6({8{1'b0}}),
    .in_7({8{1'b0}}), .out(multiplexer_1_out));
  Multiplexer #(.Selector_Bits(3), .Bits(8)) multiplexer_2 (
    .sel(SEL), .in_0({8{1'b0}}), .in_1({8{1'b0}}), .in_2(multiplicador_8bits_1_mq),
    .in_3(divisor_8bits_1_mq), .in_4({8{1'b0}}), .in_5({8{1'b0}}), .in_6({8{1'b0}}), .in_7({8{1'b0}}),
    .out(multiplexer_2_out));
  register_8bits register_8bits_1 (.D(multiplexer_1_out), .CLK(CLK), .Q(AC));
  register_8bits register_8bits_2 (.D(multiplexer_2_out), .CLK(CLK), .Q(MQ));
endmodule
