// Digital circuit cpu_simples.dig as structural Verilog
module cpu_simples (
  input  CLK,
  output [7:0] AC,
  output [7:0] MQ
);

  wire [2:0] \Operações_d ;
  wire [7:0] counter_1_out, Operandos_d;

  Counter #(.Bits(8), .isProgramCounter("true")) counter_1 (
    .en(1'b1), .C(CLK), .clr(1'b0), .out(counter_1_out));  // open: ovf
  ROM #(.AddrBits(8), .Bits(3)) \Operações  (.A(counter_1_out), .sel(1'b1), .D(\Operações_d ));
  ROM #(.AddrBits(8), .Bits(8)) Operandos (.A(counter_1_out), .sel(1'b1), .D(Operandos_d));
  ALU alu_1 (.AC_in(AC), .N(Operandos_d), .SEL(\Operações_d ), .CLK(CLK), .AC(AC), .MQ(MQ));

  // Notes on the sheet:
  //   contents of Operações (hex, n*v repeats v):
  //   0,1,2,3,4,5
  //   contents of Operandos (hex, n*v repeats v):
  //   14,0,1,3
endmodule
