// Digital circuit divisor_8bits.dig as structural Verilog
module divisor_8bits (
  input  [7:0] AC,
  input  [7:0] N,
  output [7:0] Resto,
  output [7:0] MQ
);

  wire [7:0] passo_div_1_p_out, passo_div_2_p_out, passo_div_3_p_out, passo_div_4_p_out, passo_div_5_p_out,
       passo_div_6_p_out, passo_div_7_p_out;

  passo_div passo_div_1 (.A_i(AC[7]), .P_in({8{1'b0}}), .N(N), .P_out(passo_div_1_p_out), .Q_i(MQ[7]));
  passo_div passo_div_2 (.A_i(AC[6]), .P_in(passo_div_1_p_out), .N(N), .P_out(passo_div_2_p_out), .Q_i(MQ[6]));
  passo_div passo_div_3 (.A_i(AC[5]), .P_in(passo_div_2_p_out), .N(N), .P_out(passo_div_3_p_out), .Q_i(MQ[5]));
  passo_div passo_div_4 (.A_i(AC[4]), .P_in(passo_div_3_p_out), .N(N), .P_out(passo_div_4_p_out), .Q_i(MQ[4]));
  passo_div passo_div_5 (.A_i(AC[3]), .P_in(passo_div_4_p_out), .N(N), .P_out(passo_div_5_p_out), .Q_i(MQ[3]));
  passo_div passo_div_6 (.A_i(AC[2]), .P_in(passo_div_5_p_out), .N(N), .P_out(passo_div_6_p_out), .Q_i(MQ[2]));
  passo_div passo_div_7 (.A_i(AC[1]), .P_in(passo_div_6_p_out), .N(N), .P_out(passo_div_7_p_out), .Q_i(MQ[1]));
  passo_div passo_div_8 (.A_i(AC[0]), .P_in(passo_div_7_p_out), .N(N), .P_out(Resto), .Q_i(MQ[0]));

  // Other names for the same wires on the sheet: AC_0 = AC[0]; AC_1 = AC[1]; AC_2 = AC[2]; AC_3 = AC[3]; AC_4 = AC[4];
  //   AC_5 = AC[5]; AC_6 = AC[6]; AC_7 = AC[7]; Q_0 = MQ[0]; Q_1 = MQ[1]; Q_2 = MQ[2]; Q_3 = MQ[3]; Q_4 = MQ[4];
  //   Q_5 = MQ[5]; Q_6 = MQ[6]; Q_7 = MQ[7]
endmodule
