// Digital circuit multiplicador_8bits.dig as structural Verilog
module multiplicador_8bits (
  input  [7:0] A,
  input  [7:0] B,
  output [7:0] AC,
  output [7:0] MQ,
  output [15:0] S
);

  wire PP0_0, PP0_1, PP0_2, PP0_3, PP0_4, PP0_5, PP0_6, PP0_7, PP1_0, PP1_1, PP1_2, PP1_3, PP1_4, PP1_5,
       PP1_6, PP1_7, PP2_0, PP2_1, PP2_2, PP2_3, PP2_4, PP2_5, PP2_6, PP2_7, PP3_0, PP3_1, PP3_2, PP3_3,
       PP3_4, PP3_5, PP3_6, PP3_7, PP4_0, PP4_1, PP4_2, PP4_3, PP4_4, PP4_5, PP4_6, PP4_7, PP5_0, PP5_1,
       PP5_2, PP5_3, PP5_4, PP5_5, PP5_6, PP5_7, PP6_0, PP6_1, PP6_2, PP6_3, PP6_4, PP6_5, PP6_6, PP6_7,
       PP7_0, PP7_1, PP7_2, PP7_3, PP7_4, PP7_5, PP7_6, PP7_7;
  wire [15:0] somador_16bits_1_s, somador_16bits_2_s, somador_16bits_3_s, somador_16bits_4_s,
       somador_16bits_5_s, somador_16bits_6_s;

  and and_1 (PP0_0, A[0], B[0]);
  and and_2 (PP0_1, A[1], B[0]);
  and and_3 (PP0_2, A[2], B[0]);
  and and_4 (PP0_3, A[3], B[0]);
  and and_5 (PP0_4, A[4], B[0]);
  and and_6 (PP0_5, A[5], B[0]);
  and and_7 (PP0_6, A[6], B[0]);
  and and_8 (PP0_7, A[7], B[0]);
  and and_9 (PP1_0, A[0], B[1]);
  and and_10 (PP1_1, A[1], B[1]);
  and and_11 (PP1_2, A[2], B[1]);
  and and_12 (PP1_3, A[3], B[1]);
  and and_13 (PP1_4, A[4], B[1]);
  and and_14 (PP1_5, A[5], B[1]);
  and and_15 (PP1_6, A[6], B[1]);
  and and_16 (PP1_7, A[7], B[1]);
  somador_16bits somador_16bits_1 (
    .Cin(1'b0), .A({{8{1'b0}}, PP0_7, PP0_6, PP0_5, PP0_4, PP0_3, PP0_2, PP0_1, PP0_0}),
    .B({{7{1'b0}}, PP1_7, PP1_6, PP1_5, PP1_4, PP1_3, PP1_2, PP1_1, PP1_0, 1'b0}), .S(somador_16bits_1_s));  // open: Cout
  and and_17 (PP2_0, A[0], B[2]);
  and and_18 (PP2_1, A[1], B[2]);
  and and_19 (PP2_2, A[2], B[2]);
  and and_20 (PP2_3, A[3], B[2]);
  and and_21 (PP2_4, A[4], B[2]);
  and and_22 (PP2_5, A[5], B[2]);
  and and_23 (PP2_6, A[6], B[2]);
  and and_24 (PP2_7, A[7], B[2]);
  somador_16bits somador_16bits_2 (
    .Cin(1'b0), .A(somador_16bits_1_s),
    .B({{6{1'b0}}, PP2_7, PP2_6, PP2_5, PP2_4, PP2_3, PP2_2, PP2_1, PP2_0, 2'b00}), .S(somador_16bits_2_s));  // open: Cout
  and and_25 (PP3_0, A[0], B[3]);
  and and_26 (PP3_1, A[1], B[3]);
  and and_27 (PP3_2, A[2], B[3]);
  and and_28 (PP3_3, A[3], B[3]);
  and and_29 (PP3_4, A[4], B[3]);
  and and_30 (PP3_5, A[5], B[3]);
  and and_31 (PP3_6, A[6], B[3]);
  and and_32 (PP3_7, A[7], B[3]);
  somador_16bits somador_16bits_3 (
    .Cin(1'b0), .A(somador_16bits_2_s),
    .B({{5{1'b0}}, PP3_7, PP3_6, PP3_5, PP3_4, PP3_3, PP3_2, PP3_1, PP3_0, 3'b000}), .S(somador_16bits_3_s));  // open: Cout
  and and_33 (PP4_0, A[0], B[4]);
  and and_34 (PP4_1, A[1], B[4]);
  and and_35 (PP4_2, A[2], B[4]);
  and and_36 (PP4_3, A[3], B[4]);
  and and_37 (PP4_4, A[4], B[4]);
  and and_38 (PP4_5, A[5], B[4]);
  and and_39 (PP4_6, A[6], B[4]);
  and and_40 (PP4_7, A[7], B[4]);
  somador_16bits somador_16bits_4 (
    .Cin(1'b0), .A(somador_16bits_3_s),
    .B({4'b0000, PP4_7, PP4_6, PP4_5, PP4_4, PP4_3, PP4_2, PP4_1, PP4_0, 4'b0000}), .S(somador_16bits_4_s));  // open: Cout
  and and_41 (PP5_0, A[0], B[5]);
  and and_42 (PP5_1, A[1], B[5]);
  and and_43 (PP5_2, A[2], B[5]);
  and and_44 (PP5_3, A[3], B[5]);
  and and_45 (PP5_4, A[4], B[5]);
  and and_46 (PP5_5, A[5], B[5]);
  and and_47 (PP5_6, A[6], B[5]);
  and and_48 (PP5_7, A[7], B[5]);
  somador_16bits somador_16bits_5 (
    .Cin(1'b0), .A(somador_16bits_4_s),
    .B({3'b000, PP5_7, PP5_6, PP5_5, PP5_4, PP5_3, PP5_2, PP5_1, PP5_0, {5{1'b0}}}), .S(somador_16bits_5_s));  // open: Cout
  and and_49 (PP6_0, A[0], B[6]);
  and and_50 (PP6_1, A[1], B[6]);
  and and_51 (PP6_2, A[2], B[6]);
  and and_52 (PP6_3, A[3], B[6]);
  and and_53 (PP6_4, A[4], B[6]);
  and and_54 (PP6_5, A[5], B[6]);
  and and_55 (PP6_6, A[6], B[6]);
  and and_56 (PP6_7, A[7], B[6]);
  somador_16bits somador_16bits_6 (
    .Cin(1'b0), .A(somador_16bits_5_s),
    .B({2'b00, PP6_7, PP6_6, PP6_5, PP6_4, PP6_3, PP6_2, PP6_1, PP6_0, {6{1'b0}}}), .S(somador_16bits_6_s));  // open: Cout
  and and_57 (PP7_0, A[0], B[7]);
  and and_58 (PP7_1, A[1], B[7]);
  and and_59 (PP7_2, A[2], B[7]);
  and and_60 (PP7_3, A[3], B[7]);
  and and_61 (PP7_4, A[4], B[7]);
  and and_62 (PP7_5, A[5], B[7]);
  and and_63 (PP7_6, A[6], B[7]);
  and and_64 (PP7_7, A[7], B[7]);
  somador_16bits somador_16bits_7 (
    .Cin(1'b0), .A(somador_16bits_6_s),
    .B({1'b0, PP7_7, PP7_6, PP7_5, PP7_4, PP7_3, PP7_2, PP7_1, PP7_0, {7{1'b0}}}), .S({MQ, AC}));  // open: Cout

  assign S = {MQ, AC};
endmodule
