// Digital circuit passo_div.dig as structural Verilog
module passo_div (
  input  A_i,
  input  [7:0] P_in,
  input  [7:0] N,
  output [7:0] P_out,
  output Q_i
);

  wire [7:0] S;

  Multiplexer #(.Bits(8)) multiplexer_1 (.sel(S[7]), .in_0(S), .in_1({P_in[6:0], A_i}), .out(P_out));
  subtrator_8bits subtrator_8bits_1 (.A({P_in[6:0], A_i}), .B(N), .S(S));  // open: Cout
  not not_1 (Q_i, S[7]);

  // Other names for the same wires on the sheet: PS[7:0] = {P_in[6:0], A_i}; S0[6:0] = S[6:0]; S1 = S[7]
endmodule
