// Digital circuit somador_16bits.dig as structural Verilog
module somador_16bits (
  input  Cin,
  input  [15:0] A,
  input  [15:0] B,
  output [15:0] S,
  output Cout
);

  wire somador_8bits_1_cout;

  somador_8bits somador_8bits_1 (.Cin(Cin), .A(A[7:0]), .B(B[7:0]), .S(S[7:0]), .Cout(somador_8bits_1_cout));
  somador_8bits somador_8bits_2 (.Cin(somador_8bits_1_cout), .A(A[15:8]), .B(B[15:8]), .S(S[15:8]), .Cout(Cout));

  // Other names for the same wires on the sheet: A0[7:0] = A[7:0]; A1[7:0] = A[15:8]; B0[7:0] = B[7:0];
  //   B1[7:0] = B[15:8]; S0[7:0] = S[7:0]; S1[7:0] = S[15:8]
endmodule
