// Digital circuit somador_1bit.dig as structural Verilog
module somador_1bit (
  input  Cin,
  input  A,
  input  B,
  output S,
  output Co
);

  wire and_1_out, and_2_out, and_3_out;

  xor xor_1 (S, A, B, Cin);
  and and_1 (and_1_out, A, B);
  and and_2 (and_2_out, A, Cin);
  and and_3 (and_3_out, B, Cin);
  or or_1 (Co, and_1_out, and_2_out, and_3_out);

  // Other names for the same wires on the sheet: Ci = Cin
endmodule
