// Digital circuit somador_8bits.dig as structural Verilog
module somador_8bits (
  input  Cin,
  input  [7:0] A,
  input  [7:0] B,
  output [7:0] S,
  output Cout
);

  wire somador_1bit_1_co, somador_1bit_2_co, somador_1bit_3_co, somador_1bit_4_co, somador_1bit_5_co,
       somador_1bit_6_co, somador_1bit_7_co;

  somador_1bit somador_1bit_1 (.Cin(Cin), .A(A[0]), .B(B[0]), .S(S[0]), .Co(somador_1bit_1_co));
  somador_1bit somador_1bit_2 (.Cin(somador_1bit_1_co), .A(A[1]), .B(B[1]), .S(S[1]), .Co(somador_1bit_2_co));
  somador_1bit somador_1bit_3 (.Cin(somador_1bit_2_co), .A(A[2]), .B(B[2]), .S(S[2]), .Co(somador_1bit_3_co));
  somador_1bit somador_1bit_4 (.Cin(somador_1bit_3_co), .A(A[3]), .B(B[3]), .S(S[3]), .Co(somador_1bit_4_co));
  somador_1bit somador_1bit_5 (.Cin(somador_1bit_4_co), .A(A[4]), .B(B[4]), .S(S[4]), .Co(somador_1bit_5_co));
  somador_1bit somador_1bit_6 (.Cin(somador_1bit_5_co), .A(A[5]), .B(B[5]), .S(S[5]), .Co(somador_1bit_6_co));
  somador_1bit somador_1bit_7 (.Cin(somador_1bit_6_co), .A(A[6]), .B(B[6]), .S(S[6]), .Co(somador_1bit_7_co));
  somador_1bit somador_1bit_8 (.Cin(somador_1bit_7_co), .A(A[7]), .B(B[7]), .S(S[7]), .Co(Cout));
endmodule
