// Digital circuit subtrator_8bits.dig as structural Verilog
module subtrator_8bits (
  input  [7:0] A,
  input  [7:0] B,
  output [7:0] S,
  output Cout
);

  wire not_1_out, not_2_out, not_3_out, not_4_out, not_5_out, not_6_out, not_7_out, not_8_out,
       somador_1bit_1_co, somador_1bit_2_co, somador_1bit_3_co, somador_1bit_4_co, somador_1bit_5_co,
       somador_1bit_6_co, somador_1bit_7_co;

  not not_1 (not_1_out, B[0]);
  not not_2 (not_2_out, B[1]);
  not not_3 (not_3_out, B[2]);
  not not_4 (not_4_out, B[3]);
  not not_5 (not_5_out, B[4]);
  not not_6 (not_6_out, B[5]);
  not not_7 (not_7_out, B[6]);
  not not_8 (not_8_out, B[7]);
  somador_1bit somador_1bit_1 (.Cin(1'b1), .A(A[0]), .B(not_1_out), .S(S[0]), .Co(somador_1bit_1_co));
  somador_1bit somador_1bit_2 (.Cin(somador_1bit_1_co), .A(A[1]), .B(not_2_out), .S(S[1]), .Co(somador_1bit_2_co));
  somador_1bit somador_1bit_3 (.Cin(somador_1bit_2_co), .A(A[2]), .B(not_3_out), .S(S[2]), .Co(somador_1bit_3_co));
  somador_1bit somador_1bit_4 (.Cin(somador_1bit_3_co), .A(A[3]), .B(not_4_out), .S(S[3]), .Co(somador_1bit_4_co));
  somador_1bit somador_1bit_5 (.Cin(somador_1bit_4_co), .A(A[4]), .B(not_5_out), .S(S[4]), .Co(somador_1bit_5_co));
  somador_1bit somador_1bit_6 (.Cin(somador_1bit_5_co), .A(A[5]), .B(not_6_out), .S(S[5]), .Co(somador_1bit_6_co));
  somador_1bit somador_1bit_7 (.Cin(somador_1bit_6_co), .A(A[6]), .B(not_7_out), .S(S[6]), .Co(somador_1bit_7_co));
  somador_1bit somador_1bit_8 (.Cin(somador_1bit_7_co), .A(A[7]), .B(not_8_out), .S(S[7]), .Co(Cout));
  LED plus (.in(S[7]));
endmodule
